// Logisim project pratica2.circ as structural Verilog: 1 circuit, main circuit main
module main (
  input  A,
  input  B,
  input  C,
  input  D,
  input  A_2,
  input  B_2,
  input  C_2,
  output out_8,
  output X
);

  wire and_1_out, and_2_out, and_3_out, and_4_out, and_5_out, not_1_out, not_2_out, not_3_out, xor_1_out;

  not not_1 (not_1_out, A);
  not not_2 (not_2_out, B_2);
  not not_3 (not_3_out, B);
  xor xor_1 (xor_1_out, A_2, not_2_out);
  and and_1 (and_1_out, A_2, C_2);
  and and_2 (and_2_out, A, B);
  and and_3 (and_3_out, not_1_out, C);
  and and_4 (and_4_out, not_3_out, C);
  and and_5 (and_5_out, B, not_3_out, D);
  or or_1 (X, xor_1_out, and_1_out);
  or or_2 (out_8, and_2_out, and_3_out, and_4_out, and_5_out);

  // Notes on the sheet:
  //   1.1
  //   1.2
endmodule
